# Fritzing sketch diagrama_esquematico_display_temp_umid (saved by Fritzing 0.9.2b)

parts:
  Componente1 = Arduino Nano (Rev3.0)
  LCD1 = LCD screen
  BMP180_Breakout1 = Barometric Pressure Sensor - BMP180 Breakout (GY-68)
  IC1 = Voltage Regulator LM1117 [package=sot223]
  J1 = Power Jack [package=power_jack_combo]
  R1 = Rotary Potentiometer (Small) [maximum_resistance=100kΩ package=THT]

nets:
  GND: Componente1.GND, LCD1.VSS
  N1: Componente1.D2, LCD1.DB7
  N2: Componente1.D3, LCD1.DB6
  N3: Componente1.D4, LCD1.DB5
  N4: Componente1.D5, LCD1.DB4
  N5: Componente1.D11/MOSI, LCD1.E
  N6: Componente1.D12/MISO, LCD1.RS
  5V: Componente1.5V, LCD1.VDD
  N7: Componente1.A5, BMP180_Breakout1.SCL
  N8: Componente1.A4, BMP180_Breakout1.SDA
  N9: Componente1.3V3, IC1.OUT
  N10: LCD1.V0, R1.wiper
  GND_2: BMP180_Breakout1.GND, IC1.ADJ, J1.GND
  N11: IC1.IN, J1.PWR

notes:
  3.3V
  5V
  GND
  Si7021
  Contraste LCD
  LCD 16x2
  Arduino Nano
